# Fritzing sketch 1006_garage_rc (saved by Fritzing 0.9.3b)
breadboards: 1

parts:
  Part1 = Arduino Uno (Rev3) - ICSP
  HC-SR04_Sensor_1 = HC-SR04 Ultrasonic Distance Sensor
  LED2 = LED - 3mm [color="Yellow (595nm)" package="3 mm [THT]"]
  LED3 = LED - 3mm [color="Red (633nm)" package="3 mm [THT]"]
  LED4 = LED - 3mm [color="Green (555nm)" package="3 mm [THT]"]
  J1 = Basic Servo
  HC-SR04_Sensor_2 = HC-SR04 Ultrasonic Distance Sensor
  R1 = Resistor [tolerance=±5% resistance=330 package="0603 [SMD]"]
  R2 = Resistor [tolerance=±5% resistance=330 package="0603 [SMD]"]
  R3 = Resistor [tolerance=±5% resistance=330 package="0603 [SMD]"]
  J2 = Piezo Speaker
  Grove1 = Grove OLED 128x96

nets:
  N1: Part1.A4/SDA, Grove1.SDA
  N2: Part1.A5/SCL, Grove1.SCL
  N3: Part1.D8, HC-SR04_Sensor_2.ECHO
  N4: Part1.D9_PWM, HC-SR04_Sensor_2.TRIG
  N5: Part1.D12/MISO, J1.pulse
  N6: Part1.D13/SCK, J2.pin2
  N7: Part1.D2, R1.Pin_1
  N8: Part1.D3_PWM, R2.Pin_1
  N9: Part1.D4, R3.Pin_1
  N10: Part1.D5_PWM, HC-SR04_Sensor_1.ECHO
  N11: Part1.D6_PWM, HC-SR04_Sensor_1.TRIG
  VCC: Part1.5V, HC-SR04_Sensor_1.VCC, J1.vcc, HC-SR04_Sensor_2.VCC, Grove1.VCC
  GND: Part1.GND, HC-SR04_Sensor_1.GND, LED2.cathode, LED4.cathode, J1.gnd, HC-SR04_Sensor_2.GND, J2.pin1, Grove1.GND
  N12: LED2.anode, R2.Pin_0
  N13: LED3.anode, R1.Pin_0
  N14: LED4.anode, R3.Pin_0
